// Logisim project nova32.circ as structural Verilog
module FullAdder (
  input  A,
  input  B,
  input  Cin,
  output Sum,
  output Cout
);

  wire and_1_out, and_2_out, X;

  xor xor_1 (X, A, B);
  and and_1 (and_1_out, A, B);
  and and_2 (and_2_out, Cin, X);
  or or_1 (Cout, and_1_out, and_2_out);
  xor xor_2 (Sum, X, Cin);
endmodule

module RegA32 (
  input  [31:0] DataIn,
  input  WriteA,
  input  Clock,
  input  Clear,
  output [7:0] A0,
  output [7:0] A1,
  output [7:0] A2,
  output [7:0] A3,
  output [31:0] AOut
);

  Register #(.width(32)) register_1 (.D(DataIn), .en(WriteA), .clk(Clock), .Q({A3, A2, A1, A0}), .clr(Clear));

  assign AOut = {A3, A2, A1, A0};
endmodule
